# Fritzing sketch arduino-schematic (saved by Fritzing 0.9.3b)
breadboards: 1

parts:
  Uno = Arduino Uno (Rev3)
  LCD1 = LCD screen
  BAT1 = LIPO-1000mAh [package=lipo-1000]
  5k_contrast_pot = TRIMPOT [package=3386u]
  Q1 = Basic FET N-Channel [package="DPak [SMD]"]
  Q2 = Basic FET N-Channel [package="DPak [SMD]"]
  Bulb = Resistor [tolerance=±5% resistance=5 package=THT]
  Bulb_2 = Resistor [tolerance=±5% resistance=5 package=THT]
  Shunt = Resistor [tolerance=±5% resistance=1 package=THT]

nets:
  N1: Uno.A0, Q1.drain, Q2.drain, Shunt.Pin_0
  N2: Uno.A1, BAT1.+, Shunt.Pin_1
  N3: Uno.D8, Q2.Gate
  N4: Uno.D9_PWM, Q1.Gate
  GND: Uno.GND, LCD1.VSS, LCD1.R/W, LCD1.LED-, BAT1.-, 5k_contrast_pot.CW, Bulb.Pin_1, Bulb_2.Pin_1
  N5: Uno.D0/RX, LCD1.RS
  N6: Uno.D1/TX, LCD1.E
  N7: Uno.D4, LCD1.DB4
  N8: Uno.D5_PWM, LCD1.DB5
  N9: Uno.D6_PWM, LCD1.DB6
  N10: Uno.D7, LCD1.DB7
  5V: Uno.5V, LCD1.VDD, LCD1.LED+, 5k_contrast_pot.CCW
  N11: LCD1.V0, 5k_contrast_pot.WIPER
  N12: Q1.source, Bulb_2.Pin_0
  N13: Q2.source, Bulb.Pin_0
