# Fritzing sketch lcd-batterymeter-schematic (saved by Fritzing 0.9.3b)
breadboards: 1

parts:
  Arduino = Arduino Uno (Rev3)
  1602 = LCD screen
  cell_for_testing = LIPO-1000mAh [package=lipo-1000]
  5k_contrast_pot = TRIMPOT [package=3386u]
  Q1 = Basic FET N-Channel [package="DPak [SMD]"]
  Q2 = Basic FET N-Channel [package="DPak [SMD]"]
  Bulb = Resistor [tolerance=±5% resistance=5 package=THT]
  Bulb_2 = Resistor [tolerance=±5% resistance=5 package=THT]
  pulldown_resistor = Resistor [tolerance=±5% resistance=10k package=THT]
  Shunt_resistor = Resistor [tolerance=±5% resistance=1 package=THT]

nets:
  N1: Arduino.A0, cell_for_testing.+, pulldown_resistor.Pin_0, Shunt_resistor.Pin_1
  N2: Arduino.A1, Bulb.Pin_0, Bulb_2.Pin_0, Shunt_resistor.Pin_0
  N3: Arduino.D8, Q2.Gate
  N4: Arduino.D9_PWM, Q1.Gate
  GND: Arduino.GND, 1602.VSS, 1602.R/W, 1602.LED-, cell_for_testing.-, 5k_contrast_pot.CW, Q1.source, Q2.source, pulldown_resistor.Pin_1
  N5: Arduino.D2, 1602.RS
  N6: Arduino.D3_PWM, 1602.E
  N7: Arduino.D4, 1602.DB4
  N8: Arduino.D5_PWM, 1602.DB5
  N9: Arduino.D6_PWM, 1602.DB6
  N10: Arduino.D7, 1602.DB7
  5V: Arduino.5V, 1602.VDD, 1602.LED+, 5k_contrast_pot.CCW
  N11: 1602.V0, 5k_contrast_pot.WIPER
  N12: Q1.drain, Bulb_2.Pin_1
  N13: Q2.drain, Bulb.Pin_1

notes:
  Power supply not shown.
  Use USB connector for power.
  Cell holder
